// Logisim project 16bitreg.circ as structural Verilog: 1 circuit, main circuit main
module main (
  input  [15:0] in_1,
  input  ENABLE,
  input  CLK,
  input  [1:0] Function_Selector
);

  wire and_1_out, and_2_out, and_3_out, and_4_out, and_5_out, and_6_out, and_7_out, and_8_out, and_9_out,
       and_10_out, and_11_out, and_12_out, and_13_out, and_14_out, multiplexer_1_out, multiplexer_2_out,
       multiplexer_3_out, multiplexer_4_out, multiplexer_5_out, multiplexer_6_out, multiplexer_7_out,
       multiplexer_8_out, multiplexer_9_out, multiplexer_10_out, multiplexer_11_out, multiplexer_12_out,
       multiplexer_13_out, multiplexer_14_out, multiplexer_15_out, multiplexer_16_out, nor_1_out, nor_2_out,
       nor_3_out, nor_4_out, nor_5_out, nor_6_out, nor_7_out, nor_8_out, nor_9_out, nor_10_out, nor_11_out,
       nor_12_out, nor_13_out, nor_14_out, not_1_out, not_2_out, not_3_out, not_4_out, not_5_out, not_6_out,
       not_7_out, not_8_out, not_9_out, not_10_out, xor_1_out, xor_2_out, xor_3_out, xor_4_out, xor_5_out,
       xor_6_out, xor_7_out, xor_8_out, xor_9_out, xor_10_out, xor_11_out, xor_12_out, xor_13_out,
       xor_14_out, xor_15_out, xor_16_out, xor_17_out, xor_18_out, xor_19_out, xor_20_out, xor_21_out,
       xor_22_out, xor_23_out, xor_24_out, xor_25_out, xor_26_out, xor_27_out, xor_28_out, xor_29_out,
       xor_30_out;
  wire [3:0] d_ff_1_q, d_ff_5_q, d_ff_9_q, d_ff_13_q;

  Hex_Digit_Display hex_digit_display_1 (.value(in_1[15:12]));  // open: dp
  Hex_Digit_Display hex_digit_display_2 (.value(in_1[11:8]));  // open: dp
  Hex_Digit_Display hex_digit_display_3 (.value(in_1[7:4]));  // open: dp
  not not_1 (not_1_out, nor_1_out);
  not not_2 (not_2_out, nor_2_out);
  not not_3 (not_3_out, nor_3_out);
  not not_4 (not_4_out, nor_4_out);
  not not_5 (not_5_out, nor_5_out);
  not not_6 (not_6_out, nor_6_out);
  not not_7 (not_7_out, nor_7_out);
  Hex_Digit_Display hex_digit_display_4 (.value(in_1[3:0]));  // open: dp
  and and_1 (and_1_out, and_9_out, d_ff_5_q[3]);
  nor nor_1 (nor_1_out, not_9_out, d_ff_5_q[3]);
  and and_2 (and_2_out, and_1_out, d_ff_9_q[0]);
  nor nor_2 (nor_2_out, not_1_out, d_ff_9_q[0]);
  and and_3 (and_3_out, and_2_out, d_ff_9_q[1]);
  nor nor_3 (nor_3_out, not_2_out, d_ff_9_q[1]);
  and and_4 (and_4_out, and_3_out, d_ff_9_q[2]);
  nor nor_4 (nor_4_out, not_3_out, d_ff_9_q[2]);
  and and_5 (and_5_out, and_4_out, d_ff_9_q[3]);
  nor nor_5 (nor_5_out, not_4_out, d_ff_9_q[3]);
  and and_6 (and_6_out, and_5_out, d_ff_13_q[0]);
  nor nor_6 (nor_6_out, not_5_out, d_ff_13_q[0]);
  and and_7 (and_7_out, and_6_out, d_ff_13_q[1]);
  nor nor_7 (nor_7_out, d_ff_13_q[1], not_6_out);
  and and_8 (and_8_out, and_7_out, d_ff_13_q[2]);
  and and_9 (and_9_out, d_ff_1_q[0], d_ff_1_q[1], d_ff_1_q[2], d_ff_5_q[2], d_ff_1_q[3], d_ff_5_q[0], d_ff_5_q[1]);
  nor nor_8 (nor_8_out, d_ff_13_q[2], not_7_out);
  xor xor_1 (xor_1_out, d_ff_1_q[0], d_ff_1_q[1]);
  not not_8 (not_8_out, d_ff_1_q[0]);
  xor xor_2 (xor_2_out, not_8_out, d_ff_1_q[1]);
  and and_10 (and_10_out, d_ff_1_q[0], d_ff_1_q[1]);
  and and_11 (and_11_out, d_ff_1_q[0], d_ff_1_q[2], d_ff_1_q[1]);
  and and_12 (and_12_out, d_ff_1_q[0], d_ff_1_q[1], d_ff_1_q[2], d_ff_1_q[3]);
  and and_13 (and_13_out, d_ff_1_q[0], d_ff_1_q[1], d_ff_1_q[2], d_ff_1_q[3], d_ff_5_q[0]);
  and and_14 (and_14_out, d_ff_1_q[0], d_ff_1_q[1], d_ff_1_q[2], d_ff_1_q[3], d_ff_5_q[0], d_ff_5_q[1]);
  nor nor_9 (nor_9_out, d_ff_1_q[0], d_ff_1_q[1], d_ff_1_q[2], d_ff_5_q[2], d_ff_1_q[3], d_ff_5_q[0], d_ff_5_q[1]);
  not not_9 (not_9_out, nor_9_out);
  xor xor_3 (xor_3_out, and_1_out, d_ff_9_q[0]);
  xor xor_4 (xor_4_out, nor_1_out, d_ff_9_q[0]);
  xor xor_5 (xor_5_out, and_2_out, d_ff_9_q[1]);
  xor xor_6 (xor_6_out, d_ff_9_q[1], nor_2_out);
  xor xor_7 (xor_7_out, and_3_out, d_ff_9_q[2]);
  xor xor_8 (xor_8_out, d_ff_9_q[2], nor_3_out);
  xor xor_9 (xor_9_out, and_4_out, d_ff_9_q[3]);
  xor xor_10 (xor_10_out, d_ff_9_q[3], nor_4_out);
  xor xor_11 (xor_11_out, and_5_out, d_ff_13_q[0]);
  xor xor_12 (xor_12_out, d_ff_13_q[0], nor_5_out);
  xor xor_13 (xor_13_out, and_6_out, d_ff_13_q[1]);
  xor xor_14 (xor_14_out, d_ff_13_q[1], nor_6_out);
  xor xor_15 (xor_15_out, and_7_out, d_ff_13_q[2]);
  xor xor_16 (xor_16_out, d_ff_13_q[2], nor_7_out);
  xor xor_17 (xor_17_out, and_8_out, d_ff_13_q[3]);
  xor xor_18 (xor_18_out, and_10_out, d_ff_1_q[2]);
  nor nor_10 (nor_10_out, d_ff_1_q[0], d_ff_1_q[1]);
  xor xor_19 (xor_19_out, nor_10_out, d_ff_1_q[2]);
  xor xor_20 (xor_20_out, and_11_out, d_ff_1_q[3]);
  nor nor_11 (nor_11_out, d_ff_1_q[0], d_ff_1_q[2], d_ff_1_q[1]);
  xor xor_21 (xor_21_out, nor_11_out, d_ff_1_q[3]);
  xor xor_22 (xor_22_out, and_12_out, d_ff_5_q[0]);
  xor xor_23 (xor_23_out, nor_12_out, d_ff_5_q[0]);
  nor nor_12 (nor_12_out, d_ff_1_q[0], d_ff_1_q[1], d_ff_1_q[2], d_ff_1_q[3]);
  xor xor_24 (xor_24_out, and_13_out, d_ff_5_q[1]);
  nor nor_13 (nor_13_out, d_ff_1_q[3], d_ff_1_q[0], d_ff_1_q[1], d_ff_1_q[2], d_ff_5_q[0]);
  xor xor_25 (xor_25_out, nor_13_out, d_ff_5_q[1]);
  xor xor_26 (xor_26_out, and_14_out, d_ff_5_q[2]);
  nor nor_14 (nor_14_out, d_ff_1_q[0], d_ff_1_q[1], d_ff_1_q[2], d_ff_1_q[3], d_ff_5_q[0], d_ff_5_q[1]);
  xor xor_27 (xor_27_out, nor_14_out, d_ff_5_q[2]);
  xor xor_28 (xor_28_out, and_9_out, d_ff_5_q[3]);
  xor xor_29 (xor_29_out, nor_9_out, d_ff_5_q[3]);
  xor xor_30 (xor_30_out, nor_8_out, d_ff_13_q[3]);
  not not_10 (not_10_out, d_ff_1_q[0]);
  Hex_Digit_Display hex_digit_display_5 (.value(d_ff_13_q));  // open: dp
  Hex_Digit_Display hex_digit_display_6 (.value(d_ff_9_q));  // open: dp
  Multiplexer #(.select(2)) multiplexer_1 (
    .in0(1'b0), .in1(in_1[0]), .in2(not_10_out), .in3(not_10_out), .out(multiplexer_1_out),
    .sel(Function_Selector));  // open: en
  Multiplexer #(.select(2)) multiplexer_2 (
    .in0(1'b0), .in1(in_1[1]), .in2(xor_1_out), .in3(xor_2_out), .out(multiplexer_2_out),
    .sel(Function_Selector));  // open: en
  Multiplexer #(.select(2)) multiplexer_3 (
    .in0(1'b0), .in1(in_1[2]), .in2(xor_18_out), .in3(xor_19_out), .out(multiplexer_3_out),
    .sel(Function_Selector));  // open: en
  Multiplexer #(.select(2)) multiplexer_4 (
    .in0(1'b0), .in1(in_1[3]), .in2(xor_20_out), .in3(xor_21_out), .out(multiplexer_4_out),
    .sel(Function_Selector));  // open: en
  Multiplexer #(.select(2)) multiplexer_5 (
    .in0(1'b0), .in1(in_1[4]), .in2(xor_22_out), .in3(xor_23_out), .out(multiplexer_5_out),
    .sel(Function_Selector));  // open: en
  Multiplexer #(.select(2)) multiplexer_6 (
    .in0(1'b0), .in1(in_1[5]), .in2(xor_24_out), .in3(xor_25_out), .out(multiplexer_6_out),
    .sel(Function_Selector));  // open: en
  Multiplexer #(.select(2)) multiplexer_7 (
    .in0(1'b0), .in1(in_1[6]), .in2(xor_26_out), .in3(xor_27_out), .out(multiplexer_7_out),
    .sel(Function_Selector));  // open: en
  Multiplexer #(.select(2)) multiplexer_8 (
    .in0(1'b0), .in1(in_1[7]), .in2(xor_28_out), .in3(xor_29_out), .out(multiplexer_8_out),
    .sel(Function_Selector));  // open: en
  Multiplexer #(.select(2)) multiplexer_9 (
    .in0(1'b0), .in1(in_1[8]), .in2(xor_3_out), .in3(xor_4_out), .out(multiplexer_9_out),
    .sel(Function_Selector));  // open: en
  Multiplexer #(.select(2)) multiplexer_10 (
    .in0(1'b0), .in1(in_1[9]), .in2(xor_5_out), .in3(xor_6_out), .out(multiplexer_10_out),
    .sel(Function_Selector));  // open: en
  Multiplexer #(.select(2)) multiplexer_11 (
    .in0(1'b0), .in1(in_1[10]), .in2(xor_7_out), .in3(xor_8_out), .out(multiplexer_11_out),
    .sel(Function_Selector));  // open: en
  Multiplexer #(.select(2)) multiplexer_12 (
    .in0(1'b0), .in1(in_1[11]), .in2(xor_9_out), .in3(xor_10_out), .out(multiplexer_12_out),
    .sel(Function_Selector));  // open: en
  Multiplexer #(.select(2)) multiplexer_13 (
    .in0(1'b0), .in1(in_1[12]), .in2(xor_11_out), .in3(xor_12_out), .out(multiplexer_13_out),
    .sel(Function_Selector));  // open: en
  Multiplexer #(.select(2)) multiplexer_14 (
    .in0(1'b0), .in1(in_1[13]), .in2(xor_13_out), .in3(xor_14_out), .out(multiplexer_14_out),
    .sel(Function_Selector));  // open: en
  Multiplexer #(.select(2)) multiplexer_15 (
    .in0(1'b0), .in1(in_1[14]), .in2(xor_15_out), .in3(xor_16_out), .out(multiplexer_15_out),
    .sel(Function_Selector));  // open: en
  Multiplexer #(.select(2)) multiplexer_16 (
    .in0(1'b0), .in1(in_1[15]), .in2(xor_17_out), .in3(xor_30_out), .out(multiplexer_16_out),
    .sel(Function_Selector));  // open: en
  Hex_Digit_Display hex_digit_display_7 (.value(d_ff_5_q));  // open: dp
  Hex_Digit_Display hex_digit_display_8 (.value(d_ff_1_q));  // open: dp
  D_Flip_Flop d_ff_1 (.clk(CLK), .D(multiplexer_1_out), .Q(d_ff_1_q[0]), .en(ENABLE));  // open: Qn, preset, reset
  D_Flip_Flop d_ff_2 (.clk(CLK), .D(multiplexer_2_out), .Q(d_ff_1_q[1]), .en(ENABLE));  // open: Qn, preset, reset
  D_Flip_Flop d_ff_3 (.clk(CLK), .D(multiplexer_3_out), .Q(d_ff_1_q[2]), .en(ENABLE));  // open: Qn, preset, reset
  D_Flip_Flop d_ff_4 (.clk(CLK), .D(multiplexer_4_out), .Q(d_ff_1_q[3]), .en(ENABLE));  // open: Qn, preset, reset
  D_Flip_Flop d_ff_5 (.clk(CLK), .D(multiplexer_5_out), .Q(d_ff_5_q[0]), .en(ENABLE));  // open: Qn, preset, reset
  D_Flip_Flop d_ff_6 (.clk(CLK), .D(multiplexer_6_out), .Q(d_ff_5_q[1]), .en(ENABLE));  // open: Qn, preset, reset
  D_Flip_Flop d_ff_7 (.clk(CLK), .D(multiplexer_7_out), .Q(d_ff_5_q[2]), .en(ENABLE));  // open: Qn, preset, reset
  D_Flip_Flop d_ff_8 (.clk(CLK), .D(multiplexer_8_out), .Q(d_ff_5_q[3]), .en(ENABLE));  // open: Qn, preset, reset
  D_Flip_Flop d_ff_9 (.clk(CLK), .D(multiplexer_9_out), .Q(d_ff_9_q[0]), .en(ENABLE));  // open: Qn, preset, reset
  D_Flip_Flop d_ff_10 (.clk(CLK), .D(multiplexer_10_out), .Q(d_ff_9_q[1]), .en(ENABLE));  // open: Qn, preset, reset
  D_Flip_Flop d_ff_11 (.clk(CLK), .D(multiplexer_11_out), .Q(d_ff_9_q[2]), .en(ENABLE));  // open: Qn, preset, reset
  D_Flip_Flop d_ff_12 (.clk(CLK), .D(multiplexer_12_out), .Q(d_ff_9_q[3]), .en(ENABLE));  // open: Qn, preset, reset
  D_Flip_Flop d_ff_13 (.clk(CLK), .D(multiplexer_13_out), .Q(d_ff_13_q[0]), .en(ENABLE));  // open: Qn, preset, reset
  D_Flip_Flop d_ff_14 (.clk(CLK), .D(multiplexer_14_out), .Q(d_ff_13_q[1]), .en(ENABLE));  // open: Qn, preset, reset
  D_Flip_Flop d_ff_15 (.clk(CLK), .D(multiplexer_15_out), .Q(d_ff_13_q[2]), .en(ENABLE));  // open: Qn, preset, reset
  D_Flip_Flop d_ff_16 (.clk(CLK), .D(multiplexer_16_out), .Q(d_ff_13_q[3]), .en(ENABLE));  // open: Qn, preset, reset

  // Notes on the sheet:
  //   INPUT
  //   REGISTER
endmodule
