// Logisim project 4regbank.circ as structural Verilog: 2 circuits, main circuit main
module main (
  input  [7:0] in_1,
  input  ENABLE,
  input  in_3,
  input  [1:0] FS,
  output [7:0] out_5
);

  wire and_1_out, and_2_out, and_3_out, and_4_out, and_5_out, and_6_out, multiplexer_1_out,
       multiplexer_2_out, multiplexer_3_out, multiplexer_4_out, multiplexer_5_out, multiplexer_6_out,
       multiplexer_7_out, multiplexer_8_out, nor_1_out, nor_2_out, nor_3_out, nor_4_out, nor_5_out,
       nor_6_out, not_1_out, not_2_out, xor_1_out, xor_2_out, xor_3_out, xor_4_out, xor_5_out, xor_6_out,
       xor_7_out, xor_8_out, xor_9_out, xor_10_out, xor_11_out, xor_12_out, xor_13_out, xor_14_out;

  Hex_Digit_Display hex_digit_display_1 (.value(in_1[7:4]));  // open: dp
  Hex_Digit_Display hex_digit_display_2 (.value(in_1[3:0]));  // open: dp
  xor xor_1 (xor_1_out, out_5[0], out_5[1]);
  not not_1 (not_1_out, out_5[0]);
  xor xor_2 (xor_2_out, not_1_out, out_5[1]);
  and and_1 (and_1_out, out_5[0], out_5[1]);
  nor nor_1 (nor_1_out, out_5[0], out_5[1]);
  and and_2 (and_2_out, out_5[0], out_5[2], out_5[1]);
  nor nor_2 (nor_2_out, out_5[0], out_5[2], out_5[1]);
  and and_3 (and_3_out, out_5[0], out_5[1], out_5[2], out_5[3]);
  nor nor_3 (nor_3_out, out_5[0], out_5[1], out_5[2], out_5[3]);
  and and_4 (and_4_out, out_5[0], out_5[1], out_5[2], out_5[3], out_5[4]);
  nor nor_4 (nor_4_out, out_5[3], out_5[0], out_5[1], out_5[2], out_5[4]);
  and and_5 (and_5_out, out_5[0], out_5[1], out_5[2], out_5[3], out_5[4], out_5[5]);
  nor nor_5 (nor_5_out, out_5[0], out_5[1], out_5[2], out_5[3], out_5[4], out_5[5]);
  and and_6 (and_6_out, out_5[0], out_5[1], out_5[2], out_5[6], out_5[3], out_5[4], out_5[5]);
  nor nor_6 (nor_6_out, out_5[0], out_5[1], out_5[2], out_5[6], out_5[3], out_5[4], out_5[5]);
  xor xor_3 (xor_3_out, and_1_out, out_5[2]);
  xor xor_4 (xor_4_out, nor_1_out, out_5[2]);
  xor xor_5 (xor_5_out, and_2_out, out_5[3]);
  xor xor_6 (xor_6_out, nor_2_out, out_5[3]);
  xor xor_7 (xor_7_out, and_3_out, out_5[4]);
  xor xor_8 (xor_8_out, nor_3_out, out_5[4]);
  xor xor_9 (xor_9_out, and_4_out, out_5[5]);
  xor xor_10 (xor_10_out, nor_4_out, out_5[5]);
  xor xor_11 (xor_11_out, and_5_out, out_5[6]);
  xor xor_12 (xor_12_out, nor_5_out, out_5[6]);
  xor xor_13 (xor_13_out, and_6_out, out_5[7]);
  xor xor_14 (xor_14_out, nor_6_out, out_5[7]);
  not not_2 (not_2_out, out_5[0]);
  Multiplexer #(.select(2)) multiplexer_1 (
    .in0(1'b0), .in1(in_1[0]), .in2(not_2_out), .in3(not_2_out), .out(multiplexer_1_out), .sel(FS));  // open: en
  Multiplexer #(.select(2)) multiplexer_2 (
    .in0(1'b0), .in1(in_1[1]), .in2(xor_1_out), .in3(xor_2_out), .out(multiplexer_2_out), .sel(FS));  // open: en
  Multiplexer #(.select(2)) multiplexer_3 (
    .in0(1'b0), .in1(in_1[2]), .in2(xor_3_out), .in3(xor_4_out), .out(multiplexer_3_out), .sel(FS));  // open: en
  Multiplexer #(.select(2)) multiplexer_4 (
    .in0(1'b0), .in1(in_1[3]), .in2(xor_5_out), .in3(xor_6_out), .out(multiplexer_4_out), .sel(FS));  // open: en
  Multiplexer #(.select(2)) multiplexer_5 (
    .in0(1'b0), .in1(in_1[4]), .in2(xor_7_out), .in3(xor_8_out), .out(multiplexer_5_out), .sel(FS));  // open: en
  Multiplexer #(.select(2)) multiplexer_6 (
    .in0(1'b0), .in1(in_1[5]), .in2(xor_9_out), .in3(xor_10_out), .out(multiplexer_6_out), .sel(FS));  // open: en
  Multiplexer #(.select(2)) multiplexer_7 (
    .in0(1'b0), .in1(in_1[6]), .in2(xor_11_out), .in3(xor_12_out), .out(multiplexer_7_out), .sel(FS));  // open: en
  Multiplexer #(.select(2)) multiplexer_8 (
    .in0(1'b0), .in1(in_1[7]), .in2(xor_13_out), .in3(xor_14_out), .out(multiplexer_8_out), .sel(FS));  // open: en
  D_Flip_Flop d_ff_1 (.clk(in_3), .D(multiplexer_1_out), .Q(out_5[0]), .en(ENABLE));  // open: Qn, preset, reset
  D_Flip_Flop d_ff_2 (.clk(in_3), .D(multiplexer_2_out), .Q(out_5[1]), .en(ENABLE));  // open: Qn, preset, reset
  D_Flip_Flop d_ff_3 (.clk(in_3), .D(multiplexer_3_out), .Q(out_5[2]), .en(ENABLE));  // open: Qn, preset, reset
  D_Flip_Flop d_ff_4 (.clk(in_3), .D(multiplexer_4_out), .Q(out_5[3]), .en(ENABLE));  // open: Qn, preset, reset
  D_Flip_Flop d_ff_5 (.clk(in_3), .D(multiplexer_5_out), .Q(out_5[4]), .en(ENABLE));  // open: Qn, preset, reset
  D_Flip_Flop d_ff_6 (.clk(in_3), .D(multiplexer_6_out), .Q(out_5[5]), .en(ENABLE));  // open: Qn, preset, reset
  D_Flip_Flop d_ff_7 (.clk(in_3), .D(multiplexer_7_out), .Q(out_5[6]), .en(ENABLE));  // open: Qn, preset, reset
  D_Flip_Flop d_ff_8 (.clk(in_3), .D(multiplexer_8_out), .Q(out_5[7]), .en(ENABLE));  // open: Qn, preset, reset
  Hex_Digit_Display hex_digit_display_3 (.value(out_5[7:4]));  // open: dp
  Hex_Digit_Display hex_digit_display_4 (.value(out_5[3:0]));  // open: dp
endmodule

module _3_register_bank (
  input  [3:0] RegSel,
  input  CLK,
  input  [7:0] in_3,
  input  [1:0] Funsel,
  input  [1:0] OutCSel,
  input  [1:0] OutDSel,
  output [7:0] out_7,
  output [7:0] out_8
);

  wire [7:0] main_1_out_5, main_2_out_5, main_3_out_5, main_4_out_5;

  Hex_Digit_Display hex_digit_display_1 (.value(in_3[7:4]));  // open: dp
  Hex_Digit_Display hex_digit_display_2 (.value(in_3[3:0]));  // open: dp
  main main_1 (.in_1(in_3), .ENABLE(RegSel[0]), .in_3(CLK), .FS(Funsel), .out_5(main_1_out_5));
  main main_2 (.in_1(in_3), .ENABLE(RegSel[1]), .in_3(CLK), .FS(Funsel), .out_5(main_2_out_5));
  main main_3 (.in_1(in_3), .ENABLE(RegSel[2]), .in_3(CLK), .FS(Funsel), .out_5(main_3_out_5));
  main main_4 (.in_1(in_3), .ENABLE(RegSel[3]), .in_3(CLK), .FS(Funsel), .out_5(main_4_out_5));
  Multiplexer #(.select(2), .width(8), .enable("false")) multiplexer_1 (
    .in0(main_1_out_5), .in1(main_2_out_5), .in2(main_3_out_5), .in3(main_4_out_5), .out(out_7), .sel(OutCSel));
  Multiplexer #(.select(2), .width(8), .enable("false")) multiplexer_2 (
    .in0(main_1_out_5), .in1(main_2_out_5), .in2(main_3_out_5), .in3(main_4_out_5), .out(out_8), .sel(OutDSel));
  Hex_Digit_Display hex_digit_display_3 (.value(out_7[7:4]));  // open: dp
  Hex_Digit_Display hex_digit_display_4 (.value(out_7[3:0]));  // open: dp
  Hex_Digit_Display hex_digit_display_5 (.value(out_8[3:0]));  // open: dp
  Hex_Digit_Display hex_digit_display_6 (.value(out_8[7:4]));  // open: dp

  // Notes on the sheet:
  //   Input
  //   PC
  //   AR
  //   SP
  //   OutC
  //   OutD
endmodule
