// Logisim project circuit.circ as structural Verilog: 7 circuits, main circuit main
module main (
  input  [7:0] in_1,
  input  [1:0] in_2,
  input  in_3,
  output [7:0] out_4
);

  wire clock_1_out;

  Clock clock_1 (.out(clock_1_out));
  _8_bit_register u_8_bit_register_1 (.in_1(in_3), .FunSel(in_2), .Input(in_1), .Q(out_4), .in_3(clock_1_out));
  _8_bit_register u_8_bit_register_2 ();  // open: in_1, FunSel, Input, Q, in_3
  _8_bit_register u_8_bit_register_3 ();  // open: in_1, FunSel, Input, Q, in_3
endmodule

module _16_bit_register (
  input  in_1,
  input  [1:0] in_2,
  input  [7:0] in_3,
  input  in_4,
  input  in_5,
  input  in_6,
  input  in_7,
  input  in_8,
  input  in_9,
  input  in_10,
  input  in_11
);

  wire and_1_out, and_2_out, and_3_out, and_4_out, and_5_out, and_6_out, clock_1_out, multiplexer_1_out,
       multiplexer_2_out, multiplexer_3_out, multiplexer_4_out, multiplexer_5_out, multiplexer_6_out,
       multiplexer_7_out, multiplexer_8_out, not_1_out, not_2_out, not_3_out, not_4_out, not_5_out,
       not_6_out, not_7_out, not_8_out, or_1_out, or_2_out, or_3_out, or_4_out, or_5_out, or_6_out,
       xor_1_out, xor_2_out, xor_3_out, xor_4_out, xor_5_out, xor_6_out, xor_7_out, xor_8_out, xor_9_out,
       xor_10_out, xor_11_out, xor_12_out, xor_13_out, xor_14_out;
  wire [7:0] d_ff_1_q;

  Hex_Digit_Display hex_digit_display_1 (.value(in_3[7:4]));  // open: dp
  Hex_Digit_Display hex_digit_display_2 (.value(in_3[3:0]));  // open: dp
  and and_1 (and_1_out, d_ff_1_q[0], d_ff_1_q[1]);
  or or_1 (or_1_out, d_ff_1_q[1], d_ff_1_q[0]);
  not not_1 (not_1_out, or_1_out);
  and and_2 (and_2_out, d_ff_1_q[0], d_ff_1_q[1], d_ff_1_q[2]);
  not not_2 (not_2_out, or_2_out);
  or or_2 (or_2_out, d_ff_1_q[0], d_ff_1_q[1], d_ff_1_q[2]);
  and and_3 (and_3_out, d_ff_1_q[0], d_ff_1_q[1], d_ff_1_q[2], d_ff_1_q[3]);
  or or_3 (or_3_out, d_ff_1_q[0], d_ff_1_q[1], d_ff_1_q[2], d_ff_1_q[3]);
  not not_3 (not_3_out, or_3_out);
  not not_4 (not_4_out, d_ff_1_q[0]);
  xor xor_1 (xor_1_out, and_1_out, d_ff_1_q[2]);
  xor xor_2 (xor_2_out, not_1_out, d_ff_1_q[2]);
  xor xor_3 (xor_3_out, and_2_out, d_ff_1_q[3]);
  xor xor_4 (xor_4_out, not_2_out, d_ff_1_q[3]);
  xor xor_5 (xor_5_out, and_3_out, d_ff_1_q[4]);
  xor xor_6 (xor_6_out, not_3_out, d_ff_1_q[4]);
  and and_4 (and_4_out, d_ff_1_q[0], d_ff_1_q[1], d_ff_1_q[2], d_ff_1_q[3], d_ff_1_q[4]);
  or or_4 (or_4_out, d_ff_1_q[0], d_ff_1_q[1], d_ff_1_q[2], d_ff_1_q[3], d_ff_1_q[4]);
  not not_5 (not_5_out, or_4_out);
  and and_5 (and_5_out, d_ff_1_q[0], d_ff_1_q[1], d_ff_1_q[2], d_ff_1_q[3], d_ff_1_q[4], d_ff_1_q[5]);
  or or_5 (or_5_out, d_ff_1_q[0], d_ff_1_q[1], d_ff_1_q[2], d_ff_1_q[3], d_ff_1_q[4], d_ff_1_q[5]);
  not not_6 (not_6_out, or_5_out);
  and and_6 (and_6_out, d_ff_1_q[0], d_ff_1_q[1], d_ff_1_q[2], d_ff_1_q[3], d_ff_1_q[4], d_ff_1_q[5], d_ff_1_q[6]);
  not not_7 (not_7_out, or_6_out);
  or or_6 (or_6_out, d_ff_1_q[0], d_ff_1_q[1], d_ff_1_q[2], d_ff_1_q[3], d_ff_1_q[4], d_ff_1_q[5], d_ff_1_q[6]);
  xor xor_7 (xor_7_out, d_ff_1_q[0], d_ff_1_q[1]);
  xor xor_8 (xor_8_out, not_4_out, d_ff_1_q[1]);
  xor xor_9 (xor_9_out, and_4_out, d_ff_1_q[5]);
  xor xor_10 (xor_10_out, d_ff_1_q[5], not_5_out);
  xor xor_11 (xor_11_out, and_5_out, d_ff_1_q[6]);
  xor xor_12 (xor_12_out, d_ff_1_q[6], not_6_out);
  xor xor_13 (xor_13_out, and_6_out, d_ff_1_q[7]);
  xor xor_14 (xor_14_out, d_ff_1_q[7], not_7_out);
  not not_8 (not_8_out, d_ff_1_q[0]);
  Multiplexer #(.select(2), .enable("false")) multiplexer_1 (
    .in0(in_4), .in1(in_3[0]), .in2(not_8_out), .in3(not_8_out), .out(multiplexer_1_out), .sel(in_2));
  Multiplexer #(.select(2), .enable("false")) multiplexer_2 (
    .in0(in_5), .in1(in_3[1]), .in2(xor_7_out), .in3(xor_8_out), .out(multiplexer_2_out), .sel(in_2));
  Multiplexer #(.select(2), .enable("false")) multiplexer_3 (
    .in0(in_6), .in1(in_3[2]), .in2(xor_1_out), .in3(xor_2_out), .out(multiplexer_3_out), .sel(in_2));
  Multiplexer #(.select(2), .enable("false")) multiplexer_4 (
    .in0(in_7), .in1(in_3[3]), .in2(xor_3_out), .in3(xor_4_out), .out(multiplexer_4_out), .sel(in_2));
  Multiplexer #(.select(2), .enable("false")) multiplexer_5 (
    .in0(in_8), .in1(in_3[4]), .in2(xor_5_out), .in3(xor_6_out), .out(multiplexer_5_out), .sel(in_2));
  Multiplexer #(.select(2), .enable("false")) multiplexer_6 (
    .in0(in_9), .in1(in_3[5]), .in2(xor_9_out), .in3(xor_10_out), .out(multiplexer_6_out), .sel(in_2));
  Multiplexer #(.select(2), .enable("false")) multiplexer_7 (
    .in0(in_10), .in1(in_3[6]), .in2(xor_11_out), .in3(xor_12_out), .out(multiplexer_7_out), .sel(in_2));
  Multiplexer #(.select(2), .enable("false")) multiplexer_8 (
    .in0(in_11), .in1(in_3[7]), .in2(xor_13_out), .in3(xor_14_out), .out(multiplexer_8_out), .sel(in_2));
  Clock clock_1 (.out(clock_1_out));
  D_Flip_Flop #(.enable("true")) d_ff_1 (
    .clk(clock_1_out), .D(multiplexer_1_out), .Q(d_ff_1_q[0]), .en(in_1));  // open: Qn, preset, reset
  D_Flip_Flop #(.enable("true")) d_ff_2 (
    .clk(clock_1_out), .D(multiplexer_2_out), .Q(d_ff_1_q[1]), .en(in_1));  // open: Qn, preset, reset
  D_Flip_Flop #(.enable("true")) d_ff_3 (
    .clk(clock_1_out), .D(multiplexer_3_out), .Q(d_ff_1_q[2]), .en(in_1));  // open: Qn, preset, reset
  D_Flip_Flop #(.enable("true")) d_ff_4 (
    .clk(clock_1_out), .D(multiplexer_4_out), .Q(d_ff_1_q[3]), .en(in_1));  // open: Qn, preset, reset
  D_Flip_Flop #(.enable("true")) d_ff_5 (
    .clk(clock_1_out), .D(multiplexer_5_out), .Q(d_ff_1_q[4]), .en(in_1));  // open: Qn, preset, reset
  D_Flip_Flop #(.enable("true")) d_ff_6 (
    .clk(clock_1_out), .D(multiplexer_6_out), .Q(d_ff_1_q[5]), .en(in_1));  // open: Qn, preset, reset
  D_Flip_Flop #(.enable("true")) d_ff_7 (
    .clk(clock_1_out), .D(multiplexer_7_out), .Q(d_ff_1_q[6]), .en(in_1));  // open: Qn, preset, reset
  D_Flip_Flop #(.enable("true")) d_ff_8 (
    .clk(clock_1_out), .D(multiplexer_8_out), .Q(d_ff_1_q[7]), .en(in_1));  // open: Qn, preset, reset
  Hex_Digit_Display hex_digit_display_3 (.value(d_ff_1_q[7:4]));  // open: dp
  Hex_Digit_Display hex_digit_display_4 (.value(d_ff_1_q[3:0]));  // open: dp
endmodule

// 8BR
module _8_bit_register (
  input  in_1,
  input  [1:0] FunSel,
  input  in_3,
  input  [7:0] Input,
  output [7:0] Q
);

  wire and_1_out, and_2_out, and_3_out, and_4_out, and_5_out, and_6_out, multiplexer_1_out,
       multiplexer_2_out, multiplexer_3_out, multiplexer_4_out, multiplexer_5_out, multiplexer_6_out,
       multiplexer_7_out, multiplexer_8_out, not_1_out, not_2_out, not_3_out, not_4_out, not_5_out,
       not_6_out, not_7_out, not_8_out, or_1_out, or_2_out, or_3_out, or_4_out, or_5_out, or_6_out,
       xor_1_out, xor_2_out, xor_3_out, xor_4_out, xor_5_out, xor_6_out, xor_7_out, xor_8_out, xor_9_out,
       xor_10_out, xor_11_out, xor_12_out, xor_13_out, xor_14_out;

  Hex_Digit_Display hex_digit_display_1 (.value(Input[7:4]));  // open: dp
  Hex_Digit_Display hex_digit_display_2 (.value(Input[3:0]));  // open: dp
  and and_1 (and_1_out, Q[0], Q[1]);
  or or_1 (or_1_out, Q[1], Q[0]);
  not not_1 (not_1_out, or_1_out);
  and and_2 (and_2_out, Q[0], Q[1], Q[2]);
  not not_2 (not_2_out, or_2_out);
  or or_2 (or_2_out, Q[0], Q[1], Q[2]);
  and and_3 (and_3_out, Q[0], Q[1], Q[2], Q[3]);
  not not_3 (not_3_out, or_3_out);
  or or_3 (or_3_out, Q[0], Q[1], Q[2], Q[3]);
  not not_4 (not_4_out, Q[0]);
  xor xor_1 (xor_1_out, and_1_out, Q[2]);
  xor xor_2 (xor_2_out, not_1_out, Q[2]);
  xor xor_3 (xor_3_out, and_2_out, Q[3]);
  xor xor_4 (xor_4_out, not_2_out, Q[3]);
  xor xor_5 (xor_5_out, and_3_out, Q[4]);
  xor xor_6 (xor_6_out, not_3_out, Q[4]);
  and and_4 (and_4_out, Q[0], Q[1], Q[2], Q[3], Q[4]);
  not not_5 (not_5_out, or_4_out);
  or or_4 (or_4_out, Q[0], Q[1], Q[2], Q[3], Q[4]);
  and and_5 (and_5_out, Q[0], Q[1], Q[2], Q[3], Q[4], Q[5]);
  or or_5 (or_5_out, Q[0], Q[1], Q[2], Q[3], Q[4], Q[5]);
  not not_6 (not_6_out, or_5_out);
  and and_6 (and_6_out, Q[0], Q[1], Q[2], Q[3], Q[4], Q[5], Q[6]);
  not not_7 (not_7_out, or_6_out);
  or or_6 (or_6_out, Q[0], Q[1], Q[2], Q[3], Q[4], Q[5], Q[6]);
  xor xor_7 (xor_7_out, Q[0], Q[1]);
  xor xor_8 (xor_8_out, not_4_out, Q[1]);
  xor xor_9 (xor_9_out, and_4_out, Q[5]);
  xor xor_10 (xor_10_out, Q[5], not_5_out);
  xor xor_11 (xor_11_out, and_5_out, Q[6]);
  xor xor_12 (xor_12_out, Q[6], not_6_out);
  xor xor_13 (xor_13_out, and_6_out, Q[7]);
  xor xor_14 (xor_14_out, Q[7], not_7_out);
  not not_8 (not_8_out, Q[0]);
  Multiplexer #(.select(2), .enable("false")) multiplexer_1 (
    .in0(1'b0), .in1(Input[0]), .in2(not_8_out), .in3(not_8_out), .out(multiplexer_1_out), .sel(FunSel));
  Multiplexer #(.select(2), .enable("false")) multiplexer_2 (
    .in0(1'b0), .in1(Input[1]), .in2(xor_7_out), .in3(xor_8_out), .out(multiplexer_2_out), .sel(FunSel));
  Multiplexer #(.select(2), .enable("false")) multiplexer_3 (
    .in0(1'b0), .in1(Input[2]), .in2(xor_1_out), .in3(xor_2_out), .out(multiplexer_3_out), .sel(FunSel));
  Multiplexer #(.select(2), .enable("false")) multiplexer_4 (
    .in0(1'b0), .in1(Input[3]), .in2(xor_3_out), .in3(xor_4_out), .out(multiplexer_4_out), .sel(FunSel));
  Multiplexer #(.select(2), .enable("false")) multiplexer_5 (
    .in0(1'b0), .in1(Input[4]), .in2(xor_5_out), .in3(xor_6_out), .out(multiplexer_5_out), .sel(FunSel));
  Multiplexer #(.select(2), .enable("false")) multiplexer_6 (
    .in0(1'b0), .in1(Input[5]), .in2(xor_9_out), .in3(xor_10_out), .out(multiplexer_6_out), .sel(FunSel));
  Multiplexer #(.select(2), .enable("false")) multiplexer_7 (
    .in0(1'b0), .in1(Input[6]), .in2(xor_11_out), .in3(xor_12_out), .out(multiplexer_7_out), .sel(FunSel));
  Multiplexer #(.select(2), .enable("false")) multiplexer_8 (
    .in0(1'b0), .in1(Input[7]), .in2(xor_13_out), .in3(xor_14_out), .out(multiplexer_8_out), .sel(FunSel));
  D_Flip_Flop #(.enable("true")) d_ff_1 (
    .clk(in_3), .D(multiplexer_1_out), .Q(Q[0]), .en(in_1));  // open: Qn, preset, reset
  D_Flip_Flop #(.enable("true")) d_ff_2 (
    .clk(in_3), .D(multiplexer_2_out), .Q(Q[1]), .en(in_1));  // open: Qn, preset, reset
  D_Flip_Flop #(.enable("true")) d_ff_3 (
    .clk(in_3), .D(multiplexer_3_out), .Q(Q[2]), .en(in_1));  // open: Qn, preset, reset
  D_Flip_Flop #(.enable("true")) d_ff_4 (
    .clk(in_3), .D(multiplexer_4_out), .Q(Q[3]), .en(in_1));  // open: Qn, preset, reset
  D_Flip_Flop #(.enable("true")) d_ff_5 (
    .clk(in_3), .D(multiplexer_5_out), .Q(Q[4]), .en(in_1));  // open: Qn, preset, reset
  D_Flip_Flop #(.enable("true")) d_ff_6 (
    .clk(in_3), .D(multiplexer_6_out), .Q(Q[5]), .en(in_1));  // open: Qn, preset, reset
  D_Flip_Flop #(.enable("true")) d_ff_7 (
    .clk(in_3), .D(multiplexer_7_out), .Q(Q[6]), .en(in_1));  // open: Qn, preset, reset
  D_Flip_Flop #(.enable("true")) d_ff_8 (
    .clk(in_3), .D(multiplexer_8_out), .Q(Q[7]), .en(in_1));  // open: Qn, preset, reset
  Hex_Digit_Display hex_digit_display_3 (.value(Q[3:0]));  // open: dp
  Hex_Digit_Display hex_digit_display_4 (.value(Q[7:4]));  // open: dp
endmodule

module _2c (
  input  in_1,
  input  [7:0] in_2,
  input  [1:0] in_3,
  input  in_4,
  output [15:0] out_5
);

  wire [1:0] multiplexer_1_out;

  Multiplexer #(.select(2), .width(2), .enable("false")) multiplexer_1 (
    .in0(2'b00), .out(multiplexer_1_out), .sel(in_3));  // open: in1, in2, in3
  _8_bit_register u_8_bit_register_1 (
    .in_1(in_4), .FunSel(multiplexer_1_out), .Input(in_2), .Q(out_5[15:8]), .in_3(in_1));
  _8_bit_register u_8_bit_register_2 (
    .in_1(in_4), .FunSel(multiplexer_1_out), .Q(out_5[7:0]), .in_3(in_1));  // open: Input
endmodule

module ect (
);

  _8_bit_register u_8_bit_register_1 ();  // open: in_1, FunSel, Input, Q, in_3
endmodule

// asdasda
module register_bank_1 (
  input  [3:0] RegSel,
  input  CLK,
  input  [7:0] in_3,
  input  [1:0] Funsel,
  input  [1:0] OutASel,
  input  [1:0] OutBSel,
  output [7:0] out_7,
  output [7:0] out_8
);

  wire [7:0] n8_bit_register_1_q, n8_bit_register_2_q, n8_bit_register_3_q, n8_bit_register_4_q;

  _8_bit_register u_8_bit_register_1 (
    .in_1(RegSel[0]), .FunSel(Funsel), .Input(in_3), .Q(n8_bit_register_1_q), .in_3(CLK));
  _8_bit_register u_8_bit_register_2 (
    .in_1(RegSel[1]), .FunSel(Funsel), .Input(in_3), .Q(n8_bit_register_2_q), .in_3(CLK));
  _8_bit_register u_8_bit_register_3 (
    .in_1(RegSel[2]), .FunSel(Funsel), .Input(in_3), .Q(n8_bit_register_3_q), .in_3(CLK));
  _8_bit_register u_8_bit_register_4 (
    .in_1(RegSel[3]), .FunSel(Funsel), .Input(in_3), .Q(n8_bit_register_4_q), .in_3(CLK));
  Multiplexer #(.select(2), .width(8), .enable("false")) multiplexer_1 (
    .in0(n8_bit_register_1_q), .in1(n8_bit_register_2_q), .in2(n8_bit_register_3_q),
    .in3(n8_bit_register_4_q), .out(out_7), .sel(OutASel));
  Multiplexer #(.select(2), .width(8), .enable("false")) multiplexer_2 (
    .in0(n8_bit_register_1_q), .in1(n8_bit_register_2_q), .in2(n8_bit_register_3_q),
    .in3(n8_bit_register_4_q), .out(out_8), .sel(OutBSel));
  Hex_Digit_Display hex_digit_display_1 (.value(out_7[7:4]));  // open: dp
  Hex_Digit_Display hex_digit_display_2 (.value(out_7[3:0]));  // open: dp
  Hex_Digit_Display hex_digit_display_3 (.value(out_8[7:4]));  // open: dp
  Hex_Digit_Display hex_digit_display_4 (.value(out_8[3:0]));  // open: dp

  // Notes on the sheet:
  //   Input
  //   OutA
  //   OutB
endmodule

module register_bank_2 (
  input  [3:0] RegSel,
  input  CLK,
  input  [7:0] in_3,
  input  [1:0] Funsel,
  input  [1:0] OutCSel,
  input  [1:0] OutDSel,
  output [7:0] out_7,
  output [7:0] out_8
);

  wire [7:0] n8_bit_register_1_q, n8_bit_register_2_q, n8_bit_register_3_q;

  Hex_Digit_Display hex_digit_display_1 (.value(in_3[3:0]));  // open: dp
  Hex_Digit_Display hex_digit_display_2 (.value(in_3[7:4]));  // open: dp
  _8_bit_register u_8_bit_register_1 (
    .in_1(RegSel[0]), .FunSel(Funsel), .Input(in_3), .Q(n8_bit_register_1_q), .in_3(CLK));
  _8_bit_register u_8_bit_register_2 (
    .in_1(RegSel[1]), .FunSel(Funsel), .Input(in_3), .Q(n8_bit_register_2_q), .in_3(CLK));
  _8_bit_register u_8_bit_register_3 (
    .in_1(RegSel[2]), .FunSel(Funsel), .Input(in_3), .Q(n8_bit_register_3_q), .in_3(CLK));
  Multiplexer #(.select(2), .width(8), .enable("false")) multiplexer_1 (
    .in0(n8_bit_register_1_q), .in1(n8_bit_register_2_q), .in2(n8_bit_register_3_q),
    .in3(n8_bit_register_1_q), .out(out_7), .sel(OutCSel));
  Multiplexer #(.select(2), .width(8), .enable("false")) multiplexer_2 (
    .in0(n8_bit_register_1_q), .in1(n8_bit_register_2_q), .in2(n8_bit_register_3_q),
    .in3(n8_bit_register_1_q), .out(out_8), .sel(OutDSel));
  Hex_Digit_Display hex_digit_display_3 (.value(out_7[7:4]));  // open: dp
  Hex_Digit_Display hex_digit_display_4 (.value(out_7[3:0]));  // open: dp
  Hex_Digit_Display hex_digit_display_5 (.value(out_8[3:0]));  // open: dp
  Hex_Digit_Display hex_digit_display_6 (.value(out_8[7:4]));  // open: dp

  // Notes on the sheet:
  //   Input
  //   PC
  //   AR
  //   SP
  //   OutC
  //   OutD
endmodule
