// Logisim project demo.circ as structural Verilog: 1 circuit, main circuit main
module main (
  input  [7:0] in_1,
  input  [1:0] in_2,
  input  in_3,
  input  [15:0] in_4,
  input  [1:0] in_5,
  input  in_6,
  input  [3:0] in_7,
  input  [7:0] in_8,
  input  [1:0] in_9,
  input  [1:0] in_10,
  input  [1:0] in_11,
  input  [3:0] in_12,
  input  [7:0] in_13,
  input  [1:0] in_14,
  input  [1:0] in_15,
  input  [1:0] in_16,
  input  [7:0] in_17,
  input  in_18,
  input  [1:0] in_19,
  input  in_20,
  output [7:0] out_21,
  output [15:0] out_22,
  output [7:0] out_23,
  output [7:0] out_24,
  output [7:0] out_25,
  output [7:0] out_26,
  output [15:0] out_27
);

  wire clock_1_out, clock_2_out, clock_3_out, clock_4_out, clock_5_out;

  Hex_Digit_Display hex_digit_display_1 (.value(in_4[15:12]));  // open: dp
  Hex_Digit_Display hex_digit_display_2 (.value(in_1[7:4]));  // open: dp
  Hex_Digit_Display hex_digit_display_3 (.value(in_1[3:0]));  // open: dp
  Hex_Digit_Display hex_digit_display_4 (.value(in_4[11:8]));  // open: dp
  Hex_Digit_Display hex_digit_display_5 (.value(in_8[7:4]));  // open: dp
  Hex_Digit_Display hex_digit_display_6 (.value(in_13[7:4]));  // open: dp
  Hex_Digit_Display hex_digit_display_7 (.value(in_17[7:4]));  // open: dp
  Hex_Digit_Display hex_digit_display_8 (.value(in_4[3:0]));  // open: dp
  Hex_Digit_Display hex_digit_display_9 (.value(in_4[7:4]));  // open: dp
  Hex_Digit_Display hex_digit_display_10 (.value(in_8[3:0]));  // open: dp
  Hex_Digit_Display hex_digit_display_11 (.value(in_13[3:0]));  // open: dp
  Hex_Digit_Display hex_digit_display_12 (.value(in_17[3:0]));  // open: dp
  Clock clock_1 (.out(clock_1_out));
  Clock clock_2 (.out(clock_2_out));
  Clock clock_3 (.out(clock_3_out));
  // _3_register_bank 3_register_bank_1: pin names not known; wires that end beside it: in_10, clock_3_out, in_11, out_23, out_24
  Clock clock_4 (.out(clock_4_out));
  // _3_register_bank 3_register_bank_2: pin names not known; wires that end beside it: in_15, clock_4_out, in_16, out_25, out_26
  Clock clock_5 (.out(clock_5_out));
  // _2c_main main_1: pin names not known; wires that end beside it: clock_5_out, in_20, out_27
  _8bitreg_main main_2 (.in_1(in_1), .ENABLE(in_3), .CLOCK(clock_1_out), .FS(in_2), .out_5(out_21));
  _16bitreg_main main_3 (.in_1(in_4), .ENABLE(in_6), .CLK(clock_2_out), .Function_Selector(in_5), .out_5(out_22));
  Hex_Digit_Display hex_digit_display_13 (.value(out_27[15:12]));  // open: dp
  Hex_Digit_Display hex_digit_display_14 (.value(out_27[7:4]));  // open: dp
  Hex_Digit_Display hex_digit_display_15 (.value(out_27[11:8]));  // open: dp
  Hex_Digit_Display hex_digit_display_16 (.value(out_21[7:4]));  // open: dp
  Hex_Digit_Display hex_digit_display_17 (.value(out_22[15:12]));  // open: dp
  Hex_Digit_Display hex_digit_display_18 (.value(out_23[7:4]));  // open: dp
  Hex_Digit_Display hex_digit_display_19 (.value(out_24[7:4]));  // open: dp
  Hex_Digit_Display hex_digit_display_20 (.value(out_25[7:4]));  // open: dp
  Hex_Digit_Display hex_digit_display_21 (.value(out_26[7:4]));  // open: dp
  Hex_Digit_Display hex_digit_display_22 (.value(out_27[3:0]));  // open: dp
  Hex_Digit_Display hex_digit_display_23 (.value(out_21[3:0]));  // open: dp
  Hex_Digit_Display hex_digit_display_24 (.value(out_22[11:8]));  // open: dp
  Hex_Digit_Display hex_digit_display_25 (.value(out_23[3:0]));  // open: dp
  Hex_Digit_Display hex_digit_display_26 (.value(out_24[3:0]));  // open: dp
  Hex_Digit_Display hex_digit_display_27 (.value(out_25[3:0]));  // open: dp
  Hex_Digit_Display hex_digit_display_28 (.value(out_26[3:0]));  // open: dp
  Hex_Digit_Display hex_digit_display_29 (.value(out_22[7:4]));  // open: dp
  Hex_Digit_Display hex_digit_display_30 (.value(out_22[3:0]));  // open: dp

  // Notes on the sheet:
  //   PART 1.1 / 8 BIT REGISTER
  //   PART 2.A / 4 REGISTER BANK
  //   PART 2.B / 3 REGISTER BANK
  //   PART 2.C / IR REGISTER
  //   PART 1.2 / 16 BIT REGISTER
endmodule
