// Logisim project part2cdeneme.circ as structural Verilog: 1 circuit, main circuit main
module main (
  input  [7:0] \input ,
  input  LH,
  input  [1:0] FS,
  input  in_4,
  input  E,
  input  in_6,
  output [7:0] out_7,
  output [15:0] out_8,
  output [7:0] out_9
);

  wire and_1_out, clock_1_out, decoder_1_out0, decoder_1_out1, decoder_1_out2, decoder_1_out3,
       decoder_2_out0, decoder_2_out1, or_1_out, or_2_out, or_3_out;
  wire [1:0] multiplexer_1_out;

  Decoder #(.select(2)) decoder_1 (
    .out0(decoder_1_out0), .out1(decoder_1_out1), .out2(decoder_1_out2), .out3(decoder_1_out3), .sel(FS));  // open: en
  Decoder decoder_2 (.out0(decoder_2_out0), .out1(decoder_2_out1), .sel(LH), .en(decoder_1_out3));
  or or_1 (or_1_out, decoder_1_out0, decoder_1_out1, decoder_1_out2);
  Clock clock_1 (.out(clock_1_out));
  and and_1 (and_1_out, or_1_out, E);
  Multiplexer #(.select(2), .width(2)) multiplexer_1 (
    .in0(2'b00), .in1(2'b10), .in2(2'b11), .in3(2'b01), .out(multiplexer_1_out), .sel(FS), .en(in_6));
  or or_2 (or_2_out, decoder_2_out1, and_1_out);
  or or_3 (or_3_out, decoder_2_out0, and_1_out);
  _8bitreg_main main_1 (.in_1(\input ), .ENABLE(or_2_out), .in_3(clock_1_out), .FS(2'b01), .out_5(out_9));
  _8bitreg_main main_2 (.in_1(\input ), .ENABLE(or_3_out), .in_3(clock_1_out), .FS(2'b01), .out_5(out_7));
  _16bitreg_main main_3 (
    .in_1({out_9, out_7}), .ENABLE(in_4), .CLK(clock_1_out), .Function_Selector(multiplexer_1_out),
    .out_5(out_8));
endmodule
